# Fritzing sketch hex-reader (saved by Fritzing 0.9.10b)
breadboards: 1

parts:
  Part1 = Arduino Nano (Rev3.0)
  U1 = 74HC165 [part_number=SN74LS165 package="DIP16 [THT]"]
  U2 = 74HC165 [part_number=SN74LS165 package="DIP16 [THT]"]
  R1 = Resistor [tolerance=±5% power=0.25 resistance=10k package=THT]
  R2 = Resistor [tolerance=±5% power=0.25 resistance=10k package=THT]
  R3 = Resistor [tolerance=±5% power=0.25 resistance=10k package=THT]
  R4 = Resistor [tolerance=±5% power=0.25 resistance=10k package=THT]
  JP3 = Header 4 [package=jst-4-pth]
  R5 = Resistor [tolerance=±5% power=0.25 resistance=10k package=THT]
  R6 = Resistor [tolerance=±5% power=0.25 resistance=10k package=THT]
  R7 = Resistor [tolerance=±5% power=0.25 resistance=10k package=THT]
  R8 = Resistor [tolerance=±5% power=0.25 resistance=10k package=THT]
  JP4 = Header 4 [package=jst-4-pth]
  R9 = Resistor [tolerance=±5% power=0.25 resistance=10k package=THT]
  R10 = Resistor [tolerance=±5% power=0.25 resistance=10k package=THT]
  R11 = Resistor [tolerance=±5% power=0.25 resistance=10k package=THT]
  R12 = Resistor [tolerance=±5% power=0.25 resistance=10k package=THT]
  JP5 = Header 4 [package=jst-4-pth]
  R13 = Resistor [tolerance=±5% power=0.25 resistance=10k package=THT]
  R14 = Resistor [tolerance=±5% power=0.25 resistance=10k package=THT]
  R15 = Resistor [tolerance=±5% power=0.25 resistance=10k package=THT]
  R16 = Resistor [tolerance=±5% power=0.25 resistance=10k package=THT]
  JP6 = Header 4 [package=jst-4-pth]
  SSD1306_OLED_Display = Grove OLED 128x96

nets:
  GND: Part1.GND, U1.GND, U1.MR, U1.Q0, U2.GND, U2.Q0, R1.Pin_1, R2.Pin_1, R3.Pin_1, R4.Pin_1, R5.Pin_0, R6.Pin_0, R7.Pin_0, R8.Pin_0, R9.Pin_0, R10.Pin_0, R11.Pin_0, R12.Pin_0, R13.Pin_1, R14.Pin_1, R15.Pin_1, R16.Pin_1, SSD1306_OLED_Display.GND
  N1: Part1.D2, U1.Q2, U2.Q2
  N2: Part1.D3, U1.Q1, U2.Q1
  5V: Part1.5V, U1.VCC, U2.VCC, SSD1306_OLED_Display.VCC
  N3: Part1.A5, SSD1306_OLED_Display.SCL
  N4: Part1.A4, SSD1306_OLED_Display.SDA
  N5: U1.Q3, R5.Pin_1, JP4.1
  N6: U1.Q4, R6.Pin_1, JP4.2
  N7: U1.Q5, R7.Pin_1, JP4.3
  N8: U1.Q6, R8.Pin_1, JP4.4
  N9: U1.Q7', U2.MR
  N10: U1.SH_CP, R4.Pin_0, JP3.1
  N11: U1.ST_CP, R3.Pin_0, JP3.2
  N12: U1.OE, R2.Pin_0, JP3.3
  N13: U1.DS, R1.Pin_0, JP3.4
  N14: U2.Q3, R9.Pin_1, JP5.1
  N15: U2.Q4, R10.Pin_1, JP5.2
  N16: U2.Q5, R11.Pin_1, JP5.3
  N17: U2.Q6, R12.Pin_1, JP5.4
  N18: U2.SH_CP, R14.Pin_0, JP6.1
  N19: U2.ST_CP, R16.Pin_0, JP6.2
  N20: U2.OE, R15.Pin_0, JP6.3
  N21: U2.DS, R13.Pin_0, JP6.4

notes:
  Probes
  PISO Shift Register
  I2C

custom parts:
  74HC165: 8-bit parallel-load shift registers
