# Fritzing sketch perf-board (saved by Fritzing 0.9.10b)
perfboards: 1

parts:
  J10 = shrouded pin header, 8 pins [form="♂ (shrouded male)"]
  J11 = shrouded pin header, 8 pins [form="♂ (shrouded male)"]
  J12 = shrouded pin header, 8 pins [form="♂ (shrouded male)"]
  J13 = shrouded pin header, 8 pins [form="♂ (shrouded male)"]  # not connected
  R141 = Resistor [tolerance=±5% power=0.25 resistance=10k package=THT]
  R142 = Resistor [tolerance=±5% power=0.25 resistance=10k package=THT]
  R143 = Resistor [tolerance=±5% power=0.25 resistance=10k package=THT]
  R144 = Resistor [tolerance=±5% power=0.25 resistance=10k package=THT]
  R145 = Resistor [tolerance=±5% power=0.25 resistance=10k package=THT]
  o2 = Module display OLED I2C 128x64 SSD1306 [package=THT]
  U7 = atmega328 [package=dip]
  R146 = Resistor [tolerance=±5% power=0.25 resistance=10k package=THT]
  R147 = Resistor [tolerance=±5% power=0.25 resistance=10k package=THT]
  R148 = Resistor [tolerance=±5% power=0.25 resistance=10k package=THT]
  J14 = female pin header, 2 pins [form="♀ (female)"]  # not connected
  J15 = female pin header, 2 pins [form="♀ (female)"]  # not connected
  S5 = Momentary Switch [package=ksa_sealed_tac_switch]
  Y4 = CRYSTAL [package=crystal-smd-5x3]
  S6 = Momentary Switch [package=ksa_sealed_tac_switch]
  S7 = Momentary Switch [package=ksa_sealed_tac_switch]
  C6 = Capacitor [package=cap-pth-small2]
  C7 = Capacitor [package=cap-pth-small2]
  R149 = Resistor [tolerance=±5% power=0.25 resistance=220 package=THT]
  R150 = Resistor [tolerance=±5% power=0.25 resistance=220 package=THT]
  R151 = Resistor [tolerance=±5% power=0.25 resistance=220 package=THT]
  LED2 = LED - 3mm [color="Red (633nm)" current=0.030 package="3 mm [THT]"]
  R152 = Resistor [tolerance=±5% power=0.25 resistance=10k package=THT]
  R153 = Resistor [tolerance=±5% power=0.25 resistance=10k package=THT]
  R154 = Resistor [tolerance=±5% power=0.25 resistance=10k package=THT]
  R155 = Resistor [tolerance=±5% power=0.25 resistance=10k package=THT]
  R156 = Resistor [tolerance=±5% power=0.25 resistance=10k package=THT]
  R157 = Resistor [tolerance=±5% power=0.25 resistance=10k package=THT]
  R158 = Resistor [tolerance=±5% power=0.25 resistance=10k package=THT]
  R159 = Resistor [tolerance=±5% power=0.25 resistance=10k package=THT]
  R160 = Resistor [tolerance=±5% power=0.25 resistance=10k package=THT]
  R161 = Resistor [tolerance=±5% power=0.25 resistance=10k package=THT]
  R162 = Resistor [tolerance=±5% power=0.25 resistance=10k package=THT]
  R163 = Resistor [tolerance=±5% power=0.25 resistance=10k package=THT]
  R164 = Resistor [tolerance=±5% power=0.25 resistance=10k package=THT]
  R165 = Resistor [tolerance=±5% power=0.25 resistance=10k package=THT]
  R166 = Resistor [tolerance=±5% power=0.25 resistance=10k package=THT]
  R167 = Resistor [tolerance=±5% power=0.25 resistance=10k package=THT]
  R168 = Resistor [tolerance=±5% power=0.25 resistance=10k package=THT]
  R177 = Resistor [tolerance=±5% power=0.25 resistance=10k package=THT]
  R178 = Resistor [tolerance=±5% power=0.25 resistance=10k package=THT]
  R179 = Resistor [tolerance=±5% power=0.25 resistance=10k package=THT]
  R180 = Resistor [tolerance=±5% power=0.25 resistance=10k package=THT]
  R181 = Resistor [tolerance=±5% power=0.25 resistance=10k package=THT]
  R182 = Resistor [tolerance=±5% power=0.25 resistance=10k package=THT]
  R183 = Resistor [tolerance=±5% power=0.25 resistance=10k package=THT]
  R184 = Resistor [tolerance=±5% power=0.25 resistance=10k package=THT]
  J16 = female pin header, 6 pins [form="♀ (female)"]
  74HC1 = 74HC165 [package="DIP (Dual Inline) [THT]"]
  74HC2 = 74HC165 [package="DIP (Dual Inline) [THT]"]
  74HC3 = 74HC165 [package="DIP (Dual Inline) [THT]"]
  74HC4 = 74HC165 [package="DIP (Dual Inline) [THT]"]
  C8 = Capacitor [package=cap-pth-small2]

nets (from the breadboard view):
  N1: J10.pin5, R148.Pin_0, 74HC1.D7
  N2: J10.pin6, R147.Pin_0, 74HC1.D6
  N3: J10.pin7, R146.Pin_0, 74HC1.D5
  N4: J10.pin8, R145.Pin_0, 74HC1.D4
  N5: J11.pin6, R156.Pin_0, 74HC2.D6
  N6: J12.pin1, R179.Pin_1, 74HC3.D3
  N7: J12.pin2, R177.Pin_1, 74HC3.D2
  N8: J12.pin3, R178.Pin_1, 74HC3.D1
  N9: J12.pin4, R180.Pin_1, 74HC3.D0
  N10: R141.Pin_0, R144.Pin_0, C6.2, C7.1
  N11: R141.Pin_1, 74HC1.D0
  N12: R142.Pin_1, 74HC1.D1
  N13: R143.Pin_1, 74HC1.D2
  N14: R144.Pin_1, 74HC1.D3
  N15: R145.Pin_1, R148.Pin_1
  N16: o2.SCL, U7.A5
  N17: o2.SDA, U7.A4
  N18: U7.RESET, S5.2, R149.Pin_1, C8.2
  N19: U7.D0_(RX), J16.pin3
  N20: U7.D1_(TX), J16.pin2
  N21: U7.D2, S6.1, R150.Pin_1
  N22: U7.D3_(PWM), S7.1, R151.Pin_1
  N23: U7.XLAT1, C7.2
  N24: U7.XLAT2, Y4.2, C6.1
  N25: U7.D9_(PWM), 74HC1.CP, 74HC2.CP, 74HC3.CP, 74HC4.CP
  N26: U7.D10_(PWM), 74HC1.!PL, 74HC2.!PL, 74HC3.!PL, 74HC4.!PL
  N27: U7.D11_(PWM), 74HC4.Q7
  N28: U7.D12, 74HC1.!CE, 74HC2.!CE, 74HC3.!CE, 74HC4.!CE
  VCC: S6.3, S7.3, R149.Pin_0, R152.Pin_0, J16.pin4, 74HC1.Vcc, 74HC2.Vcc, 74HC3.Vcc, 74HC4.Vcc
  N29: R150.Pin_0, R151.Pin_0
  N30: LED2.anode, R152.Pin_1
  N31: R153.Pin_0, 74HC2.D4
  N32: R153.Pin_1, R154.Pin_1
  N33: R154.Pin_0, 74HC2.D7
  N34: R155.Pin_0, 74HC2.D5
  N35: R157.Pin_0, 74HC3.D4
  N36: R157.Pin_1, R158.Pin_1
  N37: R158.Pin_0, 74HC3.D7
  N38: R159.Pin_0, 74HC3.D5
  N39: R160.Pin_0, 74HC3.D6
  N40: R161.Pin_0, 74HC4.D4
  N41: R161.Pin_1, R162.Pin_1
  N42: R162.Pin_0, 74HC4.D7
  N43: R163.Pin_0, 74HC4.D5
  N44: R164.Pin_0, 74HC4.D6
  N45: R165.Pin_0, R166.Pin_0
  N46: R165.Pin_1, 74HC4.D3
  N47: R166.Pin_1, 74HC4.D0
  N48: R167.Pin_1, 74HC4.D2
  N49: R168.Pin_1, 74HC4.D1
  N50: R179.Pin_0, R180.Pin_0
  N51: R181.Pin_1, 74HC2.D2
  N52: R182.Pin_1, 74HC2.D1
  N53: R183.Pin_0, R184.Pin_0
  N54: R183.Pin_1, 74HC2.D3
  N55: R184.Pin_1, 74HC2.D0
  N56: J16.pin1, C8.1
  GND: 74HC1.GND, 74HC2.GND, 74HC3.GND, 74HC4.GND
  N57: 74HC1.Q7, 74HC2.DS
  N58: 74HC2.Q7, 74HC3.DS
  N59: 74HC3.Q7, 74HC4.DS

notes:
  GND & VCC swapped vs the Fritzing part

custom parts:
  Module display OLED I2C 128x64 SSD1306: Ecran OLED I2C SSD163 de 128x64 avec connexion I2C
  74HC165: Asynchrounous parallel-in serial-out.
