# Fritzing sketch schematic (saved by Fritzing 0.9.10b)

parts:
  J11 = shrouded pin header, 8 pins [form="♂ (shrouded male)"]
  o2 = Module display OLED I2C 128x64 SSD1306 [package=THT]
  U7 = atmega328 [package=dip]
  J14 = female pin header, 2 pins [form="♀ (female)"]
  J15 = female pin header, 2 pins [form="♀ (female)"]
  S5 = Momentary Switch [package=ksa_sealed_tac_switch]
  Y4 = CRYSTAL [package=crystal-smd-5x3]
  S6 = Momentary Switch [package=ksa_sealed_tac_switch]
  S7 = Momentary Switch [package=ksa_sealed_tac_switch]
  LED2 = LED - 3mm [color="Red (633nm)" current=0.030 package="3 mm [THT]"]
  R152 = Resistor [tolerance=±5% power=0.25 resistance=680 package=THT]
  74HC4 = 74HC165 [package="DIP (Dual Inline) [THT]"]
  C12 = Ceramic Capacitor [capacitance=22pF voltage=35V package="100 mil [THT, multilayer]"]
  C14 = Ceramic Capacitor [capacitance=100nF voltage=35V package="100 mil [THT, multilayer]"]
  C15 = Electrolytic Capacitor [capacitance=10µF voltage=35V package="100 mil [THT, electrolytic]"]
  R185 = Resistor [tolerance=±5% power=0.25 resistance=10k package=THT]
  R188 = Resistor [tolerance=±5% power=0.25 resistance=10k package=THT]
  R189 = Resistor [tolerance=±5% power=0.25 resistance=10k package=THT]
  R190 = Resistor [tolerance=±5% power=0.25 resistance=10k package=THT]
  R191 = Resistor [tolerance=±5% power=0.25 resistance=10k package=THT]
  R192 = Resistor [tolerance=±5% power=0.25 resistance=10k package=THT]
  R193 = Resistor [tolerance=±5% power=0.25 resistance=10k package=THT]
  R194 = Resistor [tolerance=±5% power=0.25 resistance=10k package=THT]
  74HC5 = 74HC165 [package="DIP (Dual Inline) [THT]"]
  J17 = shrouded pin header, 8 pins [form="♂ (shrouded male)"]
  R195 = Resistor [tolerance=±5% power=0.25 resistance=10k package=THT]
  R196 = Resistor [tolerance=±5% power=0.25 resistance=10k package=THT]
  R197 = Resistor [tolerance=±5% power=0.25 resistance=10k package=THT]
  R198 = Resistor [tolerance=±5% power=0.25 resistance=10k package=THT]
  R199 = Resistor [tolerance=±5% power=0.25 resistance=10k package=THT]
  R200 = Resistor [tolerance=±5% power=0.25 resistance=10k package=THT]
  R201 = Resistor [tolerance=±5% power=0.25 resistance=10k package=THT]
  R202 = Resistor [tolerance=±5% power=0.25 resistance=10k package=THT]
  74HC6 = 74HC165 [package="DIP (Dual Inline) [THT]"]
  J18 = shrouded pin header, 8 pins [form="♂ (shrouded male)"]
  R203 = Resistor [tolerance=±5% power=0.25 resistance=10k package=THT]
  R204 = Resistor [tolerance=±5% power=0.25 resistance=10k package=THT]
  R205 = Resistor [tolerance=±5% power=0.25 resistance=10k package=THT]
  R206 = Resistor [tolerance=±5% power=0.25 resistance=10k package=THT]
  R207 = Resistor [tolerance=±5% power=0.25 resistance=10k package=THT]
  R208 = Resistor [tolerance=±5% power=0.25 resistance=10k package=THT]
  R209 = Resistor [tolerance=±5% power=0.25 resistance=10k package=THT]
  R210 = Resistor [tolerance=±5% power=0.25 resistance=10k package=THT]
  74HC7 = 74HC165 [package="DIP (Dual Inline) [THT]"]
  J19 = shrouded pin header, 8 pins [form="♂ (shrouded male)"]
  R211 = Resistor [tolerance=±5% power=0.25 resistance=10k package=THT]
  R212 = Resistor [tolerance=±5% power=0.25 resistance=10k package=THT]
  R213 = Resistor [tolerance=±5% power=0.25 resistance=10k package=THT]
  R214 = Resistor [tolerance=±5% power=0.25 resistance=10k package=THT]
  R215 = Resistor [tolerance=±5% power=0.25 resistance=10k package=THT]
  R216 = Resistor [tolerance=±5% power=0.25 resistance=10k package=THT]
  R217 = Resistor [tolerance=±5% power=0.25 resistance=10k package=THT]
  R218 = Resistor [tolerance=±5% power=0.25 resistance=10k package=THT]
  C17 = Ceramic Capacitor [capacitance=22pF voltage=35V package="100 mil [THT, multilayer]"]
  R219 = Resistor [tolerance=±5% power=0.25 resistance=10k package=THT]
  R220 = Resistor [tolerance=±5% power=0.25 resistance=10k package=THT]
  R221 = Resistor [tolerance=±5% power=0.25 resistance=10k package=THT]
  J10 = shrouded pin header, 6 pins [form="♂ (shrouded male)"]

nets:
  N1: J11.pin1, 74HC4.D3, R193.Pin_0
  N2: J11.pin2, 74HC4.D2, R192.Pin_0
  N3: J11.pin3, 74HC4.D1, R194.Pin_0
  N4: J11.pin4, 74HC4.D0, R191.Pin_0
  N5: J11.pin5, 74HC4.D7, R190.Pin_1
  N6: J11.pin6, 74HC4.D6, R189.Pin_1
  N7: J11.pin7, 74HC4.D5, R188.Pin_1
  N8: J11.pin8, 74HC4.D4, R185.Pin_1
  GND: o2.GND, U7.GND, J14.pin2, J15.pin1, S5.1, LED2.cathode, 74HC4.GND, C12.0, C15.-, R185.Pin_0, R188.Pin_0, R189.Pin_0, R190.Pin_0, R191.Pin_1, R192.Pin_1, R193.Pin_1, R194.Pin_1, 74HC5.GND, R195.Pin_1, R196.Pin_1, R197.Pin_0, R198.Pin_0, R199.Pin_1, R200.Pin_1, R201.Pin_0, R202.Pin_0, 74HC6.GND, R203.Pin_1, R204.Pin_0, R205.Pin_1, R206.Pin_0, R207.Pin_0, R208.Pin_1, R209.Pin_0, R210.Pin_1, 74HC7.GND, 74HC7.DS, R211.Pin_1, R212.Pin_0, R213.Pin_1, R214.Pin_0, R215.Pin_0, R216.Pin_1, R217.Pin_0, R218.Pin_1, C17.1, R219.Pin_0, R220.Pin_0, J10.pin6
  5V: o2.VCC, U7.VCC, J14.pin1, J15.pin2, S6.1, S7.1, R152.Pin_0, 74HC4.Vcc, C15.+, 74HC5.Vcc, 74HC6.Vcc, 74HC7.Vcc, R221.Pin_0, J10.pin4
  N9: o2.SCL, U7.A5
  N10: o2.SDA, U7.A4
  N11: U7.RESET, S5.3, C14.0, R221.Pin_1
  N12: U7.D0_(RX), J10.pin3
  N13: U7.D1_(TX), J10.pin2
  N14: U7.D3_(PWM), S6.3, R220.Pin_1
  N15: U7.D4, S7.3, R219.Pin_1
  N16: U7.XLAT1, Y4.1, C17.0
  N17: U7.XLAT2, Y4.2, C12.1
  N18: U7.D9_(PWM), 74HC4.Q7
  N19: U7.D10_(PWM), 74HC4.!CE, 74HC5.!CE, 74HC6.!CE, 74HC7.!CE
  N20: U7.D11_(PWM), 74HC4.CP, 74HC5.CP, 74HC6.CP, 74HC7.CP
  N21: U7.D12, 74HC4.!PL, 74HC5.!PL, 74HC6.!PL, 74HC7.!PL
  N22: LED2.anode, R152.Pin_1
  N23: 74HC4.DS, 74HC5.Q7
  N24: C14.1, J10.pin1
  N25: 74HC5.D4, J17.pin8, R198.Pin_1
  N26: 74HC5.D5, J17.pin7, R202.Pin_1
  N27: 74HC5.D6, J17.pin6, R201.Pin_1
  N28: 74HC5.D7, J17.pin5, R197.Pin_1
  N29: 74HC5.DS, 74HC6.Q7
  N30: 74HC5.D0, J17.pin4, R196.Pin_0
  N31: 74HC5.D1, J17.pin3, R200.Pin_0
  N32: 74HC5.D2, J17.pin2, R199.Pin_0
  N33: 74HC5.D3, J17.pin1, R195.Pin_0
  N34: 74HC6.D4, J18.pin8, R206.Pin_1
  N35: 74HC6.D5, J18.pin7, R209.Pin_1
  N36: 74HC6.D6, J18.pin6, R204.Pin_1
  N37: 74HC6.D7, J18.pin5, R207.Pin_1
  N38: 74HC6.DS, 74HC7.Q7
  N39: 74HC6.D0, J18.pin4, R205.Pin_0
  N40: 74HC6.D1, J18.pin3, R210.Pin_0
  N41: 74HC6.D2, J18.pin2, R203.Pin_0
  N42: 74HC6.D3, J18.pin1, R208.Pin_0
  N43: 74HC7.D4, J19.pin8, R214.Pin_1
  N44: 74HC7.D5, J19.pin7, R217.Pin_1
  N45: 74HC7.D6, J19.pin6, R212.Pin_1
  N46: 74HC7.D7, J19.pin5, R215.Pin_1
  N47: 74HC7.D0, J19.pin4, R213.Pin_0
  N48: 74HC7.D1, J19.pin3, R218.Pin_0
  N49: 74HC7.D2, J19.pin2, R211.Pin_0
  N50: 74HC7.D3, J19.pin1, R216.Pin_0

custom parts:
  Module display OLED I2C 128x64 SSD1306: Ecran OLED I2C SSD163 de 128x64 avec connexion I2C
  74HC165: Asynchrounous parallel-in serial-out.
